# Fritzing sketch simple_wheeled_robot (saved by Fritzing 0.9.3b)

parts:
  Raspberry_Pi1 = Raspberry Pi B rev2
  Part1 = Arduino Uno (Rev3)
  J1 = Basic Servo
  hc-sr1 = hc-sr04
  M3 = DC Motor  # not connected
  MD03A1 = Dual VNH2SP30 Motor Driver [part_number=MD03A]
  M4 = DC Motor  # not connected
  VCC1 = 4 x AAA Battery Mount
  LCD1 = LCD screen
  LED3 = smd LED [color="Red (635nm)" package="1206 [SMD]"]
  LED4 = smd LED [color="Red (635nm)" package="1206 [SMD]"]
  J2 = Piezo Speaker
  U1 = LIPO-2000mAh [package=lipo-2000]  # not connected
  LED5 = smd LED [color="Green (555nm)" package="1206 [SMD]"]
  LED6 = smd LED [color="Red (635nm)" package="1206 [SMD]"]
  LED7 = smd LED [color="Yellow (585nm)" package="1206 [SMD]"]
  J3 = Infrared Proximity Sensor
  J4 = Infrared Proximity Sensor
  Part2 = FTDI Basic Programmer

nets:
  5V: Raspberry_Pi1.5V, hc-sr1.VCC
  N1: Raspberry_Pi1.GPIO_2, LCD1.LED-
  N2: Raspberry_Pi1.GPIO_3, LCD1.LED+
  N3: Raspberry_Pi1.GPIO_23, hc-sr1.Trig
  N4: Raspberry_Pi1.GPIO_17, MD03A1.1INb
  N5: Raspberry_Pi1.GPIO_18, J2.pin2
  N6: Raspberry_Pi1.GPIO_4, MD03A1.1INa
  N7: Raspberry_Pi1.GPIO_24, hc-sr1.Echo
  N8: Raspberry_Pi1.GPIO_10, MD03A1.2INb#143
  N9: Raspberry_Pi1.GPIO_25, MD03A1.2INb#142
  N10: Raspberry_Pi1.GPIO_8, LED3.anode
  N11: Raspberry_Pi1.GPIO_7, LED4.anode
  GND: Raspberry_Pi1.GND, hc-sr1.GND, J2.pin1
  N12: Part1.D11_PWM/MOSI, LED5.anode
  N13: Part1.D12/MISO, LED7.anode
  N14: Part1.D13/SCK, LED6.anode
  N15: Part1.GND, LED5.cathode
  N16: Part1.D0/RX, Part2.TXO
  N17: Part1.D1/TX, Part2.RXI
  N18: Part1.D3_PWM, J4.Vout
  N19: Part1.D4, J3.Vout
  N20: Part1.D5_PWM, J1.pulse
  5V_2: Part1.5V, J1.vcc
  N21: Part1.VIN, Part2.POWER
  N22: MD03A1.VIN, VCC1.+
  N23: MD03A1.GND, VCC1.-
  N24: LED3.cathode, LED4.cathode

notes:
  直流减速电机x4
  L293D电机扩展板
  有源蜂鸣器
  FTDI转串口模块
  红外测距模块
  电机驱动板电源
